# Fritzing sketch RCPulseInJoystickServoControl (saved by Fritzing 0.9.2b)
circuit board: 8.46667cm x 5.64444cm
breadboards: 1

parts:
  IC1 = L293D [package=THT]
  Uno = Arduino Uno (Rev3) - ICSP
  M1 = DC Motor
  M2 = DC Motor
  battery_switch = SWITCH_SPDT [package=kps-1290]
  Tyranis_X8R_RX = shrouded pin header, 6 pins [form="♂ (shrouded male)"]
  U1 = RELAY [package=relay-g5q]
  VCC2 = 4 x AAA Battery Mount
  BAT1 = BC9VPC [package=bc9vpc]

nets (from the schematic view):
  N1: IC1.Enable_1, Uno.D3_PWM
  N2: IC1.In_1, Uno.D7
  N3: IC1.Out_1_(_Controlled_by_Enable_1_), M1.pin_2
  GND: IC1.0V, Uno.GND, Tyranis_X8R_RX.pin6, VCC2.-, BAT1.V-
  N4: IC1.Out_2_(_Controlled_by_Enable_1_), M1.pin_1
  N5: IC1.In_2, Uno.D8
  N6: IC1.+Vmotor, U1.NO
  N7: IC1.Enable_2, Uno.D5_PWM
  N8: IC1.In_3, Uno.D12/MISO
  N9: IC1.Out_3_(_Controlled_by_Enable_2_), M2.pin_2
  N10: IC1.Out_4_(_Controlled_by_Enable_2_), M2.pin_1
  N11: IC1.In_4, Uno.D13/SCK
  N12: IC1.+V, Uno.5V, Tyranis_X8R_RX.pin4
  N13: Uno.D9_PWM, Tyranis_X8R_RX.pin3
  N14: Uno.D10_PWM/SS, Tyranis_X8R_RX.pin2
  N15: Uno.D11_PWM/MOSI, Tyranis_X8R_RX.pin1
  N16: Uno.VIN, U1.COIL2
  N17: battery_switch.O, U1.COIL1
  N18: battery_switch.P, BAT1.V+
  N19: U1.MAIN, VCC2.+

notes:
  Frsky X8R Receiver: red=5v; black=grnd
  blue: ch1; green: ch2; yellow: ch3

// code stored in the sketch: RCPulseInJoystickServoControl.ino
/*
RC PulseIn Joystick Servo Control
by Mike Zawitkowski
created on March 19, 2016
 
Enables an Arduino based robot car to be controlled directly via
Frsky Taranis X9D Transmitter and X8R receiver.


CHANGES:
  3/19/2016 
    - Incorporated code into loop that was uncommented in tutorial
    - Swapped ch2/ch3 pins to correct incorrect mapping
    - changed serial monitor print behavior
    - Adapted to work with L293D motor controller [WORK IN PROGRESS]
   
  3/20/2016
    - Adapted to work with L293D motor controller [WORK IN PROGRESS]
    - Wiring both motor Enable triggers to a single PWM pin Out   
    - Changed move, turn variable names to avoid namespace conflict (move already exists)
    - Fixed error in channel mapping 
    - Added additional serial print statements for debugging

  3/22/2016
    - Allow left stick to be idle at zero
    - Move movement to separate function for readibility
    - Streamline conditionals
      
  TODO LIST:
    - Replace pulseIn with interrupts
    - Add the Taranis TX configuration info 
    - Include info on wiring with X8R and breadboard (fritzing?)
    - Cross-link with photos to an Instructables.com post
    - Incorporate autonomous mode
    - Run all channels into Arduino on a single wire
    - Add protection to the L293D in case of voltage drop
    

 CREDITS, THANKS, FURTHER READING:

  Attribution for the Sparkfun code, which served as a starting point:
    "RC Hobby Controllers and Arduino" by NPoole, May 22, 2012
    Retrieved on 3/19/2016 from: https://www.sparkfun.com/tutorials/348
   
    RC PulseIn Serial Read out
    By: Nick Poole
    SparkFun Electronics
    Date: 5
    License: CC-BY SA 3.0 - Creative commons share-alike 3.0
    use this code however you'd like, just keep this license and
    attribute. Let me know if you make hugely, awesome, great changes.


  To learn more about the L293D IC Dual H-bridge motor driver, check out:
    http://www.robotplatform.com/howto/L293/motor_driver_1.html
 

  I found this article very helpful to see the best approach options for PWM control:
    http://rcarduino.blogspot.com/2012/01/how-to-read-rc-receiver-with.html 
    
    
  Great stacikexchange post with lots of links, and discussion about getting all RX signals into a single input:
    http://robotics.stackexchange.com/questions/1207/read-multiple-channels-of-rx-tx-with-arduino
    

    http://blog.whatgeek.com.pt/2015/03/arduino-l293d-dc-motors-control/    

*/
 

// Channels are the RX in to the Arduino. These will be PWM pins
int ch1; // Left stick is on/off
int ch2; // Forward/Backward
int ch3; // Left/Right

int moveVal; // Forward/Back speed (formerly move but that appears to be already in the namespace)
int turnVal; // Turning Factor

// The L293D IC controls 2 motors, and for each has 2 control pins and 1 enable pin
// The enable pin will be referred to as pwm_a and pwm_b
int pwm_a = 3;  //PWM control for motor outputs 
int pwm_b = 5;  //PWM control for motor outputs

// direction control for motor outputs, non-PWM
int dir_a1 = 7;
int dir_a2 = 8;
int dir_b1 = 12;
int dir_b2 = 13;


void setup() {

  pinMode(9, INPUT); // Set our channel input pins as such
  pinMode(10, INPUT);
  pinMode(11, INPUT);
  
  Serial.begin(9600); // Pour a bowl of Serial (for debugging)

  pinMode(pwm_a, OUTPUT);  //Set control pins to be outputs
  pinMode(pwm_b, OUTPUT);

  pinMode(dir_a1, OUTPUT);
  pinMode(dir_a2, OUTPUT);
  pinMode(dir_b1, OUTPUT);
  pinMode(dir_b2, OUTPUT);

  analogWrite(pwm_a, 0);  
  analogWrite(pwm_b, 0);
}


void loop() {
  
  // Read pulse width of each channel
  ch1 = pulseIn(9, HIGH, 25000); // Left stick (engaged/disengaged)

  // Only run the loop when ch1 is Engaged
  if (ch1 > 1000) {
    ch2 = pulseIn(11, HIGH, 25000); // Right stick up/down NOTE the swapped pins
    moveVal = map(ch2, 1000, 2000, -1000, 1000); //center over zero
    moveVal = constrain(moveVal, -255, 255);   //only pass values whose absolutes are
                                               //valid pwm values
    if (abs(moveVal)) < 10 {

      moveVal = 0;
      fullStop();

    } else {
      
      ch3 = pulseIn(10, HIGH, 25000); // Right stick left/right NOTE the swapped pins
      turnVal = map(ch3,1000,2000,-500,500);
      turnVal = constrain(turnVal, -255, 255);
      movement(moveVal, turnVal);

    };                                                                                                                                                                                                                                                                                                                                                                                      
}


void movement(int moveVal, int turnVal) {
  if (moveVal > 0) {          // if moveVal is positive
    moveForward();  // then we move forward
  } else {          // if moveVal is negative
    moveBackward();          // we move backward
    moveVal = abs(moveVal);   // but now switch it to a positive int for the next step
  };
  
  /*This is where we do some mixing, by subtracting our "turn" 
  variable from the appropriate motor's speed we can execute
  a turn in either direction*/
  if (turnVal > 0) {
    analogWrite(pwm_b, moveVal - turnVal); 
    analogWrite(pwm_a, moveVal);
  } else {
    turnVal = abs(turnVal); 
    analogWrite(pwm_a, moveVal - turnVal); 
    analogWrite(pwm_b, moveVal);
  };
}

void moveForward() {
    digitalWrite(dir_a1, 1);   
    digitalWrite(dir_a2, 0);   
    
    digitalWrite(dir_b1, 1);   
    digitalWrite(dir_b2, 0);   
}

void moveBackward() {
    digitalWrite(dir_a1, 0);   
    digitalWrite(dir_a2, 1);   
    
    digitalWrite(dir_b1, 0);   
    digitalWrite(dir_b2, 1);   
}


void fullStop() {
    analogWrite(pwm_a, 0);
    analogWrite(pwm_b, 0);
    digitalWrite(dir_a1, 0);   
    digitalWrite(dir_a2, 0);     
    digitalWrite(dir_b1, 0);   
    digitalWrite(dir_b2, 0);   
}

// Easier to comment out serial out content if it's a single function
void printReport() {
  if (ch1 > 1000) {
    Serial.println("Left Switch: Engaged");
  }
  if (ch1 < 1000) {
    Serial.println("Left Switch: Disengaged");
  }

  Serial.print("Right Stick X:");
  Serial.println(map(ch3, 1000,2000,-500,500));
  
  Serial.print("Right Stick Y:");
  Serial.println(map(ch2, 1000,2000,-500,500));

  Serial.print("\t\tturnVal:"); //Serial debugging stuff
  Serial.print(turnVal);
  
  Serial.print("\t\tmoveVal - turnVal:"); //Serial debugging stuff
  Serial.print(moveVal - turnVal);
  Serial.print("\n\n\n"); //Serial debugging stuff
  
  delay(800);  // The delay is great for monitoring STDOUT; but awful for real motor behavior 
}
